# Fritzing sketch dev1 (saved by Fritzing 1.0.1rc)

parts:
  WeMos_D1_Mini1 = WeMos D1 Mini
  HC-SR04_Sensor_1 = HC-SR04 Ultrasonic Distance Sensor
  HC-SR04_Sensor_2 = HC-SR04 Ultrasonic Distance Sensor
  KY-1 = Keyes Relay [package=THT]
  KY-2 = Keyes Relay [package=THT]

nets:
  VCC: WeMos_D1_Mini1.5V, HC-SR04_Sensor_1.VCC, HC-SR04_Sensor_2.VCC, KY-1.power, KY-2.power
  N1: WeMos_D1_Mini1.D1, KY-2.signal
  N2: WeMos_D1_Mini1.D2, KY-1.signal
  N3: WeMos_D1_Mini1.D5, HC-SR04_Sensor_2.TRIG
  N4: WeMos_D1_Mini1.D6, HC-SR04_Sensor_2.ECHO
  N5: WeMos_D1_Mini1.D7, HC-SR04_Sensor_1.ECHO
  N6: WeMos_D1_Mini1.D8, HC-SR04_Sensor_1.TRIG
  GND: WeMos_D1_Mini1.G, HC-SR04_Sensor_1.GND, HC-SR04_Sensor_2.GND, KY-1.ground, KY-2.ground

custom parts:
  Keyes Relay: The Keyes 5V relay module is suitable for SCM development, home appliance control. It uses a 5V~12V TIL control signal which can control DC / AC signal.
