# Fritzing sketch dev2 (saved by Fritzing 1.0.1rc)

parts:
  U1 = ESP8266 ESP-01 Upgraded WiFi Module [part_number=ESP8266]
  KY-1 = Keyes Relay [package=THT]
  YF-S201_Flow_Meter1 = YF-S201 Water Flow Meter
  VALVE1 = Plastic Solenoid Valve
  Power_plug1 = Power plug

nets:
  N1: U1.RXD, YF-S201_Flow_Meter1.SIG
  GND: U1.GND, KY-1.ground, YF-S201_Flow_Meter1.GND
  N2: U1.TXD, KY-1.signal
  N3: KY-1.power, YF-S201_Flow_Meter1.VCC
  N4: KY-1.NC, VALVE1.no_name_yet#1
  N5: KY-1.C, Power_plug1.VCC
  N6: VALVE1.no_name_yet#2, Power_plug1.GND

custom parts:
  ESP8266 ESP-01 Upgraded WiFi Module: Upgraded Version ESP-01,all Flash are upgraded to 1M byte.Also support Cloud service remote transmission.
  Keyes Relay: The Keyes 5V relay module is suitable for SCM development, home appliance control. It uses a 5V~12V TIL control signal which can control DC / AC signal.
  YF-S201 Water Flow Meter: The YF-S201 Flow Meter. The input voltage is 5V to 24V (DC).
